# Fritzing sketch connections (saved by Fritzing 0.9.3b)
breadboards: 1

parts:
  U1 = ESP8266 WiFi Module [part_number=ESP8266]
  R1 = Resistor [tolerance=±5% resistance=220 package="0603 [SMD]"]
  LED1 = LED - 3mm [color="Red (633nm)" package="3 mm [THT]"]

nets:
  N1: U1.VCC, U1.CH_PD
  N2: U1.GPIO_0, U1.GND, LED1.cathode
  N3: U1.GPIO_2, R1.Pin_1
  N4: R1.Pin_0, LED1.anode

notes:
  TX
  RX
  GND
  3,3V
  USB - TTL Serial

custom parts:
  ESP8266 WiFi Module: Generic WiFi Module based on the ESP8266 with onboard PCB antenna and UART communications
